# Fritzing sketch part3 (saved by Fritzing 0.9.3b)
breadboards: 1

parts:
  Mod1 = Raspberry Pi Pico
  GY2 = MPU-6050 Board GY-521 [form="♀ (female)" package=THT]
  Part1 = PowerBoost 500 Charger  # not connected
  USBTTL1 = USB A Plug
  USBTTL2 = Micro USB B Plug
  U1 = LIPO-1000mAh [package=lipo-1000]  # not connected
  LED1 = smd LED [color="Red (633nm)" package="0603 [SMD]"]
  R1 = Resistor [tolerance=±5% resistance=220 package="0603 [SMD]"]
  OLED2 = OLED 128x64 I2C Monochrome Display GND-VDD

nets:
  N1: Mod1.pin_3, Mod1.pin_8, Mod1.pin_13, Mod1.pin_18, Mod1.pin_23, Mod1.pin_28, Mod1.pin_33, Mod1.pin_38, Mod1.pin_42, GY2.pin2, R1.Pin_1, OLED2.GND
  N2: Mod1.pin_15, GY2.pin4, OLED2.SDA
  N3: Mod1.pin_16, GY2.pin3, OLED2.SCK
  N4: Mod1.pin_21, LED1.anode
  N5: Mod1.pin_36, GY2.pin1, OLED2.VDD
  N6: USBTTL1.usb, USBTTL2.usb
  N7: LED1.cathode, R1.Pin_0

custom parts:
  Raspberry Pi Pico: Raspberry Pi Pico. Based around the RP2040 microcontroller the Pico is a low cost microcontroller device bringing Raspberry Pi quality, cost, and easy of use to the microcontroller space. Jan 2021, Split part in to two versions: tht (this one) and SMD. This one will drill holes for a .1 in header in pcb to allow plugging in the module as well as providing pads to solder the module to the top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
  MPU-6050 Board GY-521: Acelerometro y Giroscopio MPU-6050 Board GY-521
  OLED 128x64 I2C Monochrome Display GND-VDD: OLED 128x64 I2C Monochrome Display. Note: there are two variants of this part, this one is the GND VDD SCK SDA variant. The other is VDD GND SCK SDA. Make sure you select the part that matches your module as using the incorrect part will probably destroy your module! In addition the mounting holes are marked on silkscreen but not by default drilled. If you want drilled mounting holes, copy a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
